// Digital circuit 32_bit_adder.dig as structural Verilog
module _32_bit_adder (
  input  x0,
  input  y0,
  input  x1,
  input  y1,
  input  x2,
  input  x3,
  input  y2,
  input  y3,
  input  x4,
  input  x5,
  input  x6,
  input  x7,
  input  y4,
  input  y5,
  input  y6,
  input  y7,
  input  x8,
  input  x9,
  input  x10,
  input  x11,
  input  x12,
  input  x13,
  input  x14,
  input  x15,
  input  y8,
  input  y9,
  input  y10,
  input  y11,
  input  y12,
  input  y13,
  input  y14,
  input  y15,
  input  x16,
  input  x17,
  input  x18,
  input  x19,
  input  x20,
  input  x21,
  input  x22,
  input  x23,
  input  x24,
  input  x25,
  input  x26,
  input  x27,
  input  x28,
  input  x29,
  input  x30,
  input  x31,
  input  y16,
  input  y17,
  input  y18,
  input  y19,
  input  y20,
  input  y21,
  input  y22,
  input  y23,
  input  y24,
  input  y25,
  input  y26,
  input  y27,
  input  y28,
  input  y29,
  input  y30,
  input  y31,
  output s0,
  output Overflow,
  output s1,
  output s2,
  output s3,
  output s4,
  output s5,
  output s6,
  output s7,
  output s8,
  output s9,
  output s10,
  output s11,
  output s12,
  output s13,
  output s14,
  output s15,
  output s16,
  output s17,
  output s18,
  output s19,
  output s20,
  output s21,
  output s22,
  output s23,
  output s24,
  output s25,
  output s26,
  output s27,
  output s28,
  output s29,
  output s30,
  output s31
);

  wire _8_bit_adder_2_cout, _8_bit_adder_3_cout, _8_bit_adder_4_cout;

  _8_bit_adder _8_bit_adder_1 (
    .X0(x24), .X1(x25), .X2(x26), .X3(x27), .Y0(y24), .Y1(y25), .Y2(y26), .Y3(y27), .X4(x28), .X5(x29),
    .X6(x30), .X7(x31), .Y4(y28), .Y5(y29), .Y6(y30), .Y7(y31), .Cin(_8_bit_adder_2_cout), .s0(s24),
    .s1(s25), .s2(s26), .s3(s27), .s4(s28), .s5(s29), .s6(s30), .s7(s31), .Cout(Overflow));
  _8_bit_adder _8_bit_adder_2 (
    .X0(x16), .X1(x17), .X2(x18), .X3(x19), .Y0(y16), .Y1(y17), .Y2(y18), .Y3(y19), .X4(x20), .X5(x21),
    .X6(x22), .X7(x23), .Y4(y20), .Y5(y21), .Y6(y22), .Y7(y23), .Cin(_8_bit_adder_3_cout), .s0(s16),
    .s1(s17), .s2(s18), .s3(s19), .s4(s20), .s5(s21), .s6(s22), .s7(s23), .Cout(_8_bit_adder_2_cout));
  _8_bit_adder _8_bit_adder_3 (
    .X0(x8), .X1(x9), .X2(x10), .X3(x11), .Y0(y8), .Y1(y9), .Y2(y10), .Y3(y11), .X4(x12), .X5(x13), .X6(x14),
    .X7(x15), .Y4(y12), .Y5(y13), .Y6(y14), .Y7(y15), .Cin(_8_bit_adder_4_cout), .s0(s8), .s1(s9), .s2(s10),
    .s3(s11), .s4(s12), .s5(s13), .s6(s14), .s7(s15), .Cout(_8_bit_adder_3_cout));
  _8_bit_adder _8_bit_adder_4 (
    .X0(x0), .X1(x1), .X2(x2), .X3(x3), .Y0(y0), .Y1(y1), .Y2(y2), .Y3(y3), .X4(x4), .X5(x5), .X6(x6),
    .X7(x7), .Y4(y4), .Y5(y5), .Y6(y6), .Y7(y7), .Cin(1'b0), .s0(s0), .s1(s1), .s2(s2), .s3(s3), .s4(s4),
    .s5(s5), .s6(s6), .s7(s7), .Cout(_8_bit_adder_4_cout));

  // Notes on the sheet:
  //   Michael Evan
  //   CIS-323
  //   32-Bit Binary Adder Circuit
  //   Designed from 4 custom made 8-bit circuits
  //   Light = 1
  //   Dark = 0
  //   y (binary) + x (binary) = binary result
  //   <-- binary result
  //   y-binary
  //   x-binary
  //   constant
endmodule
