// Digital circuit 4_bit_adder_subtractor.dig as structural Verilog
module _4_bit_adder_subtractor (
  input  X0,
  input  X1,
  input  X2,
  input  X3,
  input  Y0,
  input  Y1,
  input  Y2,
  input  Y3,
  input  subtract,
  output s0,
  output s1,
  output s2,
  output s3
);

  wire full_adder_2_carry, full_adder_3_carry, full_adder_4_carry, multiplexer_1_out, multiplexer_2_out,
       multiplexer_3_out, multiplexer_4_out, not_1_out, not_2_out, not_3_out, not_4_out;

  not not_1 (not_1_out, Y3);
  Multiplexer multiplexer_1 (.sel(subtract), .in_0(Y3), .in_1(not_1_out), .out(multiplexer_1_out));
  Full_Adder full_adder_1 (.x(X3), .y(multiplexer_1_out), .z(full_adder_2_carry), .sum(s3));  // open: carry
  not not_2 (not_2_out, Y2);
  Multiplexer multiplexer_2 (.sel(subtract), .in_0(Y2), .in_1(not_2_out), .out(multiplexer_2_out));
  Full_Adder full_adder_2 (.x(X2), .y(multiplexer_2_out), .z(full_adder_3_carry), .sum(s2), .carry(full_adder_2_carry));
  not not_3 (not_3_out, Y1);
  Multiplexer multiplexer_3 (.sel(subtract), .in_0(Y1), .in_1(not_3_out), .out(multiplexer_3_out));
  Full_Adder full_adder_3 (.x(X1), .y(multiplexer_3_out), .z(full_adder_4_carry), .sum(s1), .carry(full_adder_3_carry));
  not not_4 (not_4_out, Y0);
  Multiplexer multiplexer_4 (.sel(subtract), .in_0(Y0), .in_1(not_4_out), .out(multiplexer_4_out));
  Full_Adder full_adder_4 (.x(X0), .y(subtract), .z(multiplexer_4_out), .sum(s0), .carry(full_adder_4_carry));

  // Notes on the sheet:
  //   <-- binary output
  //   Michael Evan
  //   CIS-323
  //   Adder / Subtractor Circuit
  //   X - Y = OUTPUT
endmodule
