// Digital circuit 8_bit_adder.dig as structural Verilog
module _8_bit_adder (
  input  X0,
  input  X1,
  input  X2,
  input  X3,
  input  Y0,
  input  Y1,
  input  Y2,
  input  Y3,
  input  X4,
  input  X5,
  input  X6,
  input  X7,
  input  Y4,
  input  Y5,
  input  Y6,
  input  Y7,
  input  Cin,
  output s0,
  output s1,
  output s2,
  output s3,
  output s4,
  output s5,
  output s6,
  output s7,
  output Cout
);

  wire full_adder_2_carry, full_adder_3_carry, full_adder_4_carry, full_adder_5_carry, full_adder_6_carry,
       full_adder_7_carry, full_adder_8_carry;

  Full_Adder full_adder_1 (.x(X7), .y(Y7), .z(full_adder_2_carry), .sum(s7), .carry(Cout));
  Full_Adder full_adder_2 (.x(X6), .y(Y6), .z(full_adder_3_carry), .sum(s6), .carry(full_adder_2_carry));
  Full_Adder full_adder_3 (.x(X5), .y(Y5), .z(full_adder_4_carry), .sum(s5), .carry(full_adder_3_carry));
  Full_Adder full_adder_4 (.x(X4), .y(Y4), .z(full_adder_5_carry), .sum(s4), .carry(full_adder_4_carry));
  Full_Adder full_adder_5 (.x(X3), .y(Y3), .z(full_adder_6_carry), .sum(s3), .carry(full_adder_5_carry));
  Full_Adder full_adder_6 (.x(X2), .y(Y2), .z(full_adder_7_carry), .sum(s2), .carry(full_adder_6_carry));
  Full_Adder full_adder_7 (.x(X1), .y(Y1), .z(full_adder_8_carry), .sum(s1), .carry(full_adder_7_carry));
  Full_Adder full_adder_8 (.x(X0), .y(Y0), .z(Cin), .sum(s0), .carry(full_adder_8_carry));
endmodule
