// Digital circuit Final_4bit_add_sub.dig as structural Verilog
module Final_4bit_add_sub (
  input  x0,
  input  x1,
  input  x2,
  input  x3,
  input  y0,
  input  y1,
  input  y2,
  input  y3,
  input  Subtract,
  output out_1,
  output out_2,
  output out_3,
  output out_4
);

  _4_bit_adder_subtractor _4_bit_adder_subtractor_1 (
    .X0(x0), .X1(x1), .X2(x2), .X3(x3), .Y0(y0), .Y1(y1), .Y2(y2), .Y3(y3), .subtract(Subtract), .s0(out_1),
    .s1(out_2), .s2(out_3), .s3(out_4));

  // Notes on the sheet:
  //   y-binary
  //   Final 4-bit Adder/Subtractor
  //   Michael Evan
  //   CIS-323
  //   Subtraction order is x - y
  //   x-binary
endmodule
