// Digital circuit Full_Adder.dig as structural Verilog
module Full_Adder (
  input  x,
  input  y,
  input  z,
  output sum,
  output carry
);

  wire and_1_out, and_2_out, and_3_out, or_1_out, xor_1_out;

  xor xor_1 (xor_1_out, x, y);
  and and_1 (and_1_out, z, x);
  and and_2 (and_2_out, z, y);
  and and_3 (and_3_out, y, x);
  xor xor_2 (sum, xor_1_out, z);
  or or_1 (or_1_out, and_1_out, and_2_out);
  or or_2 (carry, or_1_out, and_3_out);
endmodule
